// Logisim project cpu.circ as structural Verilog: 1 circuit, main circuit main
module main (
  input  [31:0] INSTRUCTION,
  input  CLOCK,
  output [31:0] PROGRAM_COUNTER,
  output [31:0] ra,
  output [31:0] sp,
  output [31:0] t0,
  output [31:0] t1,
  output [31:0] t2,
  output [31:0] s0,
  output [31:0] s1,
  output [31:0] a0
);

  wire MemRW, RegWEn;
  wire [1:0] WBSel;
  wire [2:0] ImmSel;
  wire [3:0] ALUSel;
  wire [31:0] Imm, INSTRUCTION_Q, PC_plus_4, ReadData, Result, rs1, wb, WriteData;

  control_logic control_logic_1 (
    .RegWEn(RegWEn), .ImmSel(ImmSel), .inst(INSTRUCTION_Q), .ALUSel(ALUSel), .MemRW(MemRW), .WBSel(WBSel));  // open: BSel, ASel, BrUn, PCSel, BrLt, BrEq
  Adder #(.width(32)) adder_1 (.a(PROGRAM_COUNTER), .b(32'h4), .out(PC_plus_4));  // open: cin, cout
  Register #(.width(32)) PC (.D(PC_plus_4), .clk(CLOCK), .Q(PROGRAM_COUNTER));  // open: en, clr
  Register #(.width(32)) register_1 (.D(INSTRUCTION), .clk(CLOCK), .Q(INSTRUCTION_Q));  // open: en, clr
  imm_gen imm_gen_1 (.ImmSel(ImmSel), .inst(INSTRUCTION_Q), .imm(Imm));
  // branch_comp branch_comp_1: pin names not known
  regfile_main RegFile (
    .rd(INSTRUCTION_Q[11:7]), .Read_Data_1(rs1), .ra(ra), .sp(sp), .t0(t0), .t1(t1), .t2(t2), .s0(s0),
    .s1(s1), .a0(a0), .rs1(INSTRUCTION_Q[19:15]), .Write_Data(wb), .RegWEn(RegWEn), .clk(CLOCK));  // open: rs2, Read_Data_2
  alu Arithmetic_Logic_Unit (.ALUSel(ALUSel), .Result(Result), .A(rs1), .B(Imm));
  // mem_main DMEM: pin names not known; wires that end beside it: WriteData, CLOCK, MemRW, ReadData
  Multiplexer #(.select(2), .width(32), .enable("false")) multiplexer_1 (
    .in0(Result), .in1(ReadData), .in2(PC_plus_4), .out(wb), .sel(WBSel));  // open: in3

  // Other names for the same wires on the sheet: clk = CLOCK

  // Notes on the sheet:
  //   Output
  //   IMEM (do **NOT** move this)
  //   Inputs
  //   It is OK to move the PC, RegFile, ALU, MEM, Branch Comp, Imm Gen, and Control Logic to wherever is most convenient for you when constructing your CPU, and to delete this text
  //   Inputs/Outputs for testing. Do **NOT** move these.
endmodule
